# Fritzing sketch board (saved by Fritzing 0.9.1b)
circuit board: 7.80175cm x 2.32827cm
breadboards: 1

parts:
  part = ESP8266 Female Header [form="♀ (female)" package=THT]
  RST = Pushbutton [package=THT]
  part_2 = Battery Holders [package=battery-aa-kit]
  part_3 = Battery Holders [package=battery-aa-kit]
  Outputs1 = Outputs [form="♀ (female)" package=THT]
  PRGM = Pushbutton [package=THT]

nets:
  N1: part.TX, Outputs1.RX
  N2: part.CH_PD, part.VCC, RST.leg1, part_2.-
  N3: part.RST, RST.leg0
  N4: part.RX, Outputs1.TX
  N5: part.GPIO_0, PRGM.leg1
  N6: part.GPIO_2, Outputs1.GND
  N7: part.GND, part_3.-, Outputs1.GPIO, PRGM.leg0
  N8: part_2.+, part_3.+

notes:
  RX
  GPIO
  TX
  http://monks.co
  ESP8266

custom parts:
  ESP8266 Female Header: Female Header with pins labeled for the ESP8266 WiFi chip.
  Pushbutton: A generic pushbutton.
  Outputs: Female Header
